# Fritzing sketch read_sd_card_prototype (saved by Fritzing 0.8.7b)
breadboards: 1

parts:
  Componente1 = Arduino Uno (Rev3)
  Mod1 = KY-015 Temperature & Humidity Sensor Module [package="Breakout board"]
  SD_card_module1 = SD Card Module

nets:
  N1: Componente1.D10_PWM/SS, SD_card_module1.CS
  N2: Componente1.D11_PWM/MOSI, SD_card_module1.MOSI
  N3: Componente1.D12/MISO, SD_card_module1.MISO
  N4: Componente1.D13/SCK, SD_card_module1.SCK
  N5: Componente1.GND, Mod1.-, SD_card_module1.GND#0
  N6: Componente1.D4, Mod1.S
  N7: Componente1.3V3, SD_card_module1.+3.3
  5V: Componente1.5V, Mod1.Vin

notes:
  Pinagem Módulo SD Card
  MISO = 12
  MOSI = 11
  SCK = 13
  CS = 10
  VCC = 3.3v
  GND = GND
  Pinagem Modulo DHT11
  VCC = 5v
  GND = GND
  Signal = 4

custom parts:
  KY-015 Temperature & Humidity Sensor Module: KY-015 temperature and humidity sensor module, provides a low-latency serial interface to measure humidity and temperature.
  SD Card Module: SD Card Module Slot Socket Reader For Arduino ARM MCU
