# Fritzing sketch mqtt_publisher_to_subscriber_prototype (saved by Fritzing 0.8.7b)
breadboards: 1

parts:
  U1 = ESP32-38PinWide [part_number=ESP32-38PinWide]
  Mod1 = KY-015 Temperature & Humidity Sensor Module [package="Breakout board"]

nets:
  N1: U1.GND, Mod1.S
  VIN: U1.VIN, Mod1.Vin
  N2: U1.GPIO7, Mod1.-

notes:
  Pinagem do DHT11 no ESP32
  VCC = 5v
  GND = GND
  Signal = GPIO 27

custom parts:
  ESP32-38PinWide: Generic 38-Pin ESP32 with wide format (only access to one side of pins on a breadboard) based on Stephen Lilley's HiLetgo ESP-WROOM-32 ESP32 ESP-32S Development Board.
  KY-015 Temperature & Humidity Sensor Module: KY-015 temperature and humidity sensor module, provides a low-latency serial interface to measure humidity and temperature.
